# Fritzing sketch Schaltplan_Platine (saved by Fritzing 0.9.2b)
circuit board: 6.32635cm x 7.26452cm
breadboards: 1

parts:
  Schieberegister1 = 74HC595 [package="DIP16 [THT]"]
  Motortreiber = H-Bridge [package=THT]
  R2 = Resistor [tolerance=±5% resistance=220 package=THT]
  R3 = Resistor [tolerance=±5% resistance=220 package=THT]
  R4 = Resistor [tolerance=±5% resistance=220 package=THT]
  R5 = Resistor [tolerance=±5% resistance=220 package=THT]
  R6 = Resistor [tolerance=±5% resistance=220 package=THT]
  R7 = Resistor [tolerance=±5% resistance=220 package=THT]
  R8 = Resistor [tolerance=±5% resistance=220 package=THT]
  R1 = Resistor [tolerance=±5% resistance=220 package=THT]
  9-V-Netzteil = male pin header, 2 pins [form="♂ (male)"]
  Poti-Anschluss = male pin header, 3 pins [form="♂ (male)"]
  Motoranschluss = male pin header, 2 pins [form="♂ (male)"]
  R9 = Resistor [tolerance=±5% resistance=220 package=THT]
  R10 = Resistor [tolerance=±5% resistance=220 package=THT]
  R11 = Resistor [tolerance=±5% resistance=220 package=THT]
  R12 = Resistor [tolerance=±5% resistance=220 package=THT]
  R13 = Resistor [tolerance=±5% resistance=220 package=THT]
  R14 = Resistor [tolerance=±5% resistance=220 package=THT]
  R15 = Resistor [tolerance=±5% resistance=220 package=THT]
  R16 = Resistor [tolerance=±5% resistance=220 package=THT]
  LED-Stecker1 = longpad pin header, 10 pins [form="long pad"]
  LED-Stecker2 = longpad pin header, 10 pins [form="long pad"]
  Schieberegister2 = 74HC595 [package="DIP16 [THT]"]
  Arduino_Nano = Arduino Nano (Rev3.0)

nets (from the schematic view):
  N1: Schieberegister1.Q1, R2.Pin_1
  N2: Schieberegister1.Q2, R3.Pin_1
  N3: Schieberegister1.Q3, R4.Pin_1
  N4: Schieberegister1.Q4, R5.Pin_1
  N5: Schieberegister1.Q5, R6.Pin_1
  N6: Schieberegister1.Q6, R7.Pin_1
  N7: Schieberegister1.Q7, R8.Pin_1
  GND: Schieberegister1.GND, Schieberegister1.OE, Motortreiber.GND1, Motortreiber.GND2, 9-V-Netzteil.pin2, Poti-Anschluss.pin1, LED-Stecker1.pin2, LED-Stecker2.pin2, Schieberegister2.GND, Schieberegister2.OE, Arduino_Nano.GND
  N8: Schieberegister1.Q7', Schieberegister2.DS
  N9: Schieberegister1.SH_CP, Schieberegister2.SH_CP, Arduino_Nano.D4
  N10: Schieberegister1.ST_CP, Schieberegister2.ST_CP, Arduino_Nano.D3
  N11: Schieberegister1.DS, Arduino_Nano.D2
  N12: Schieberegister1.Q0, R1.Pin_1
  N13: Motortreiber.1_2EN, Motortreiber.VCC2, Motortreiber.VCC1, 9-V-Netzteil.pin1, Arduino_Nano.VIN
  N14: Motortreiber.1A, Arduino_Nano.D10
  N15: Motortreiber.1Y, Motoranschluss.pin1
  N16: Motortreiber.2Y, Motoranschluss.pin2
  N17: Motortreiber.2A, Arduino_Nano.D11/MOSI
  N18: R2.Pin_0, LED-Stecker1.pin9
  N19: R3.Pin_0, LED-Stecker1.pin8
  N20: R4.Pin_0, LED-Stecker1.pin7
  N21: R5.Pin_0, LED-Stecker1.pin6
  N22: R6.Pin_0, LED-Stecker1.pin5
  N23: R7.Pin_0, LED-Stecker1.pin4
  N24: R8.Pin_0, LED-Stecker1.pin3
  N25: R1.Pin_0, LED-Stecker1.pin10
  N26: Poti-Anschluss.pin2, Arduino_Nano.5V
  N27: Poti-Anschluss.pin3, Arduino_Nano.A7
  N28: R9.Pin_0, LED-Stecker2.pin10
  N29: R9.Pin_1, Schieberegister2.Q0
  N30: R10.Pin_0, LED-Stecker2.pin9
  N31: R11.Pin_0, LED-Stecker2.pin8
  N32: R12.Pin_0, LED-Stecker2.pin7
  N33: R13.Pin_0, LED-Stecker2.pin6
  N34: R14.Pin_0, LED-Stecker2.pin5
  N35: R15.Pin_0, LED-Stecker2.pin4
  N36: R16.Pin_0, LED-Stecker2.pin3
  N37: Schieberegister2.MR, Schieberegister2.VCC

// code stored in the sketch: fritzing_test.ino

