# Fritzing sketch Schieberegister_Platine (saved by Fritzing 0.9.2b)
circuit board: 10cm x 5cm
breadboards: 1

parts:
  5V-GND = male pin header, 2 pins [form="♂ (male)"]
  R1 = Resistor [tolerance=±5% resistance=220 package=THT]
  R2 = Resistor [tolerance=±5% resistance=220 package=THT]
  R3 = Resistor [tolerance=±5% resistance=220 package=THT]
  R4 = Resistor [tolerance=±5% resistance=220 package=THT]
  R5 = Resistor [tolerance=±5% resistance=220 package=THT]
  R6 = Resistor [tolerance=±5% resistance=220 package=THT]
  R7 = Resistor [tolerance=±5% resistance=220 package=THT]
  R8 = Resistor [tolerance=±5% resistance=220 package=THT]
  R9 = Resistor [tolerance=±5% resistance=220 package=THT]
  R10 = Resistor [tolerance=±5% resistance=220 package=THT]
  R11 = Resistor [tolerance=±5% resistance=220 package=THT]
  R12 = Resistor [tolerance=±5% resistance=220 package=THT]
  R13 = Resistor [tolerance=±5% resistance=220 package=THT]
  R14 = Resistor [tolerance=±5% resistance=220 package=THT]
  R15 = Resistor [tolerance=±5% resistance=220 package=THT]
  R16 = Resistor [tolerance=±5% resistance=220 package=THT]
  LED_Innen = male pin header, 10 pins [form="♂ (male)"]
  LED_Außen = male pin header, 10 pins [form="♂ (male)"]
  LED_Steuerung = male pin header, 3 pins [form="♂ (male)"]
  Schieberegister_1 = 74HC595 [package="DIP16 [THT]"]
  Schieberegister = 74HC595 [package="DIP16 [THT]"]
  Motorsteuerung = L293D [package=THT]
  GND-9V = male pin header, 2 pins [form="♂ (male)"]
  C1 = Ceramic Capacitor [capacitance=100nF package="100 mil [THT, multilayer]"]
  C2 = Ceramic Capacitor [capacitance=100nF package="100 mil [THT, multilayer]"]
  C3 = Electrolytic Capacitor [capacitance=100µF package="100 mil [THT, electrolytic]"]
  C4 = Electrolytic Capacitor [capacitance=100µF package="100 mil [THT, electrolytic]"]
  C5 = Ceramic Capacitor [capacitance=100nF package="100 mil [THT, multilayer]"]
  Motor-Ausgang = male pin header, 2 pins [form="♂ (male)"]
  Steuerung-Motor = male pin header, 2 pins [form="♂ (male)"]
  R17 = Resistor [tolerance=±5% resistance=0 package=THT]
  R18 = Resistor [tolerance=±5% resistance=0 package=THT]
  R19 = Resistor [tolerance=±5% resistance=220 package=THT]

nets:
  GND: 5V-GND.pin1, LED_Innen.pin2, LED_Außen.pin2, Schieberegister_1.GND, Schieberegister_1.OE, Schieberegister.GND, Schieberegister.OE
  N1: 5V-GND.pin2, Schieberegister_1.VCC, Schieberegister.MR, R18.Pin_1
  N2: R1.Pin_0, LED_Innen.pin9
  N3: R1.Pin_1, Schieberegister_1.Q1
  N4: R2.Pin_0, LED_Innen.pin8
  N5: R2.Pin_1, Schieberegister_1.Q2
  N6: R3.Pin_0, LED_Innen.pin10
  N7: R3.Pin_1, Schieberegister_1.Q0
  N8: R4.Pin_0, LED_Innen.pin7
  N9: R4.Pin_1, Schieberegister_1.Q3
  N10: R5.Pin_0, LED_Innen.pin6
  N11: R5.Pin_1, Schieberegister_1.Q4
  N12: R6.Pin_0, LED_Innen.pin5
  N13: R6.Pin_1, Schieberegister_1.Q5
  N14: R7.Pin_0, LED_Innen.pin4
  N15: R7.Pin_1, Schieberegister_1.Q6
  N16: R8.Pin_0, LED_Innen.pin3
  N17: R8.Pin_1, Schieberegister_1.Q7
  N18: R9.Pin_0, LED_Außen.pin9
  N19: R9.Pin_1, Schieberegister.Q1
  N20: R10.Pin_0, LED_Außen.pin8
  N21: R10.Pin_1, Schieberegister.Q2
  N22: R11.Pin_0, LED_Außen.pin7
  N23: R11.Pin_1, Schieberegister.Q3
  N24: R12.Pin_0, LED_Außen.pin6
  N25: R12.Pin_1, Schieberegister.Q4
  N26: R13.Pin_0, LED_Außen.pin5
  N27: R13.Pin_1, Schieberegister.Q5
  N28: R14.Pin_0, LED_Außen.pin4
  N29: R14.Pin_1, Schieberegister.Q6
  N30: R15.Pin_0, LED_Außen.pin3
  N31: R15.Pin_1, Schieberegister.Q7
  N32: R16.Pin_0, LED_Außen.pin10
  N33: R16.Pin_1, Schieberegister.Q0
  N34: LED_Steuerung.pin1, Schieberegister_1.DS
  N35: LED_Steuerung.pin2, Schieberegister_1.ST_CP, R17.Pin_0
  N36: LED_Steuerung.pin3, Schieberegister_1.SH_CP, Schieberegister.SH_CP
  N37: Schieberegister_1.Q7', Schieberegister.DS
  N38: Schieberegister_1.MR, Schieberegister.VCC, R18.Pin_0
  N39: Schieberegister.ST_CP, R17.Pin_1
  N40: Motorsteuerung.Enable_1, Motorsteuerung.+V, GND-9V.pin2, C4.+, C5.0
  N41: Motorsteuerung.In_1, Steuerung-Motor.pin2
  N42: Motorsteuerung.Out_1_(_Controlled_by_Enable_1_), C1.1, Motor-Ausgang.pin2
  N43: Motorsteuerung.0V, GND-9V.pin1, C1.0, C2.1, C3.-, C4.-, C5.1
  N44: Motorsteuerung.Out_2_(_Controlled_by_Enable_1_), C2.0, Motor-Ausgang.pin1
  N45: Motorsteuerung.In_2, R19.Pin_0
  N46: Motorsteuerung.+Vmotor, C3.+, R19.Pin_1
